// Logisim project dadda_mul.circ as structural Verilog: 8 circuits, main circuit main
module main (
  input  [15:0] X,
  input  [15:0] Y,
  output [16:0] PP0,
  output [16:0] PP1,
  output [16:0] PP2,
  output [16:0] PP3,
  output [16:0] PP4,
  output [16:0] PP5,
  output [16:0] PP6,
  output [16:0] PP7,
  output [31:0] Product,
  output out_12
);

  wire C_FA1_8, C_FA1_9, C_FA1_10A, C_FA1_10B, C_FA1_11A, C_FA1_11B, C_FA1_12A, C_FA1_12B, C_FA1_13A,
       C_FA1_13B, C_FA1_14, C_FA1_14A, C_FA1_14B, C_FA1_15, C_FA1_15A, C_FA1_15B, C_FA1_16, C_FA1_16A,
       C_FA1_16B, C_FA1_17, C_FA1_17A, C_FA1_17B, C_FA1_18, C_FA1_18A, C_FA1_18B, C_FA1_19, C_FA1_19A,
       C_FA1_19B, C_FA1_20A, C_FA1_20B, C_FA1_21A, C_FA1_21B, C_FA1_22A, C_FA1_22B, C_FA1_23A, C_FA1_23B,
       C_FA2_10A, C_FA2_11A, C_FA2_12A, C_FA2_13A, C_FA2_14, C_FA2_14A, C_FA2_15, C_FA2_15A, C_FA2_16,
       C_FA2_16A, C_FA2_17, C_FA2_17A, C_FA2_18, C_FA2_18A, C_FA2_19, C_FA2_19A, C_FA2_20A, C_FA2_21A,
       C_FA2_22A, C_FA2_23A, C_FA3_17, C_FA_6, C_FA_7, C_FA_8, C_FA_9, C_FA_12, C_FA_13, C_FA_20, C_FA_21,
       C_FA_24, C_FA_24B, C_FA_25, C_FA_25B, C_FA_26B, C_FA_27, C_HA_4, C_HA_5, C_HA_6, C_HA_7, C_HA_8,
       C_HA_9, C_HA_10, C_HA_11, C_HA_12, C_HA_13, C_HA_14, C_HA_15, C_HA_16, C_HA_18, C_HA_20, C_HA_22,
       C_HA_24, C_HA_26, C_HA_28, C_HA_30, full_adder_1_carry, full_adder_2_carry, full_adder_4_carry,
       full_adder_6_carry, full_adder_9_carry, full_adder_12_carry, full_adder_16_carry, full_adder_19_carry,
       full_adder_24_carry, full_adder_29_carry, full_adder_35_carry, full_adder_41_carry,
       full_adder_48_carry, full_adder_54_carry, full_adder_61_carry, full_adder_67_carry,
       full_adder_71_carry, full_adder_77_carry, full_adder_80_carry, full_adder_85_carry,
       full_adder_88_carry, full_adder_91_carry, full_adder_93_carry, full_adder_95_carry,
       full_adder_96_carry, full_adder_97_carry, half_adder_21_carry, half_adder_22_carry, N_0, N_1, N_2,
       N_3, N_4, N_5, N_6, N_7, S_FA1_8, S_FA1_9, S_FA1_10A, S_FA1_10B, S_FA1_11A, S_FA1_11B, S_FA1_12A,
       S_FA1_12B, S_FA1_13A, S_FA1_13B, S_FA1_14, S_FA1_14A, S_FA1_14B, S_FA1_15, S_FA1_15A, S_FA1_15B,
       S_FA1_16, S_FA1_16A, S_FA1_16B, S_FA1_17, S_FA1_17A, S_FA1_17B, S_FA1_18, S_FA1_18A, S_FA1_18B,
       S_FA1_19, S_FA1_19A, S_FA1_19B, S_FA1_20A, S_FA1_20B, S_FA1_21A, S_FA1_21B, S_FA1_22A, S_FA1_22B,
       S_FA1_23A, S_FA1_23B, S_FA2_10A, S_FA2_11A, S_FA2_12A, S_FA2_13A, S_FA2_14, S_FA2_14A, S_FA2_15,
       S_FA2_15A, S_FA2_16, S_FA2_16A, S_FA2_17, S_FA2_17A, S_FA2_18, S_FA2_18A, S_FA2_19, S_FA2_19A,
       S_FA2_20A, S_FA2_21A, S_FA2_22A, S_FA2_23A, S_FA3_17, S_FA_6, S_FA_7, S_FA_8, S_FA_9, S_FA_12,
       S_FA_13, S_FA_20, S_FA_21, S_FA_24, S_FA_24B, S_FA_25, S_FA_25B, S_FA_26B, S_FA_27, S_HA_4, S_HA_5,
       S_HA_6, S_HA_7, S_HA_8, S_HA_9, S_HA_10, S_HA_11, S_HA_12, S_HA_13, S_HA_14, S_HA_15, S_HA_16,
       S_HA_18, S_HA_20, S_HA_22, S_HA_24, S_HA_26, S_HA_28;
  wire [30:2] half_adder_22_sum;
  wire [31:17] not_8_out;

  Booth_row_generator booth_row_generator_1 (.Y_high(Y[1]), .Y(Y[0]), .Y_low(1'b0), .X(X), .Neg(N_0), .PP(PP0));
  Booth_row_generator booth_row_generator_2 (.Y_high(Y[3]), .Y(Y[2]), .Y_low(Y[1]), .X(X), .Neg(N_1), .PP(PP1));
  Booth_row_generator booth_row_generator_3 (.Y_high(Y[5]), .Y(Y[4]), .Y_low(Y[3]), .X(X), .Neg(N_2), .PP(PP2));
  Booth_row_generator booth_row_generator_4 (.Y_high(Y[7]), .Y(Y[6]), .Y_low(Y[5]), .X(X), .Neg(N_3), .PP(PP3));
  Booth_row_generator booth_row_generator_5 (.Y_high(Y[9]), .Y(Y[8]), .Y_low(Y[7]), .X(X), .Neg(N_4), .PP(PP4));
  Booth_row_generator booth_row_generator_6 (.Y_high(Y[11]), .Y(Y[10]), .Y_low(Y[9]), .X(X), .Neg(N_5), .PP(PP5));
  Booth_row_generator booth_row_generator_7 (.Y_high(Y[13]), .Y(Y[12]), .Y_low(Y[11]), .X(X), .Neg(N_6), .PP(PP6));
  Booth_row_generator booth_row_generator_8 (.Y_high(Y[15]), .Y(Y[14]), .Y_low(Y[13]), .X(X), .Neg(N_7), .PP(PP7));
  Half_adder half_adder_1 (.A(PP7[16]), .B(full_adder_1_carry), .Sum(half_adder_22_sum[30]), .Carry(C_HA_30));
  Full_adder full_adder_1 (
    .A(C_HA_28), .B(PP7[15]), .Cin(full_adder_2_carry), .Sum(half_adder_22_sum[29]),
    .Carry(full_adder_1_carry));
  Half_adder half_adder_2 (.A(PP7[14]), .B(C_FA_27), .Sum(S_HA_28), .Carry(C_HA_28));
  Full_adder full_adder_2 (
    .A(PP6[16]), .B(full_adder_4_carry), .Cin(S_HA_28), .Sum(half_adder_22_sum[28]),
    .Carry(full_adder_2_carry));
  Full_adder full_adder_3 (.A(C_HA_26), .B(PP7[13]), .Cin(C_FA_26B), .Sum(S_FA_27), .Carry(C_FA_27));
  Full_adder full_adder_4 (
    .A(full_adder_6_carry), .B(PP6[15]), .Cin(S_FA_27), .Sum(half_adder_22_sum[27]),
    .Carry(full_adder_4_carry));
  Half_adder half_adder_3 (.A(PP7[12]), .B(C_FA_25), .Sum(S_HA_26), .Carry(C_HA_26));
  Full_adder full_adder_5 (.A(PP6[14]), .B(C_FA_25B), .Cin(S_HA_26), .Sum(S_FA_26B), .Carry(C_FA_26B));
  Full_adder full_adder_6 (
    .A(full_adder_9_carry), .B(PP5[16]), .Cin(S_FA_26B), .Sum(half_adder_22_sum[26]),
    .Carry(full_adder_6_carry));
  Full_adder full_adder_7 (.A(C_HA_24), .B(PP7[11]), .Cin(C_FA_24), .Sum(S_FA_25), .Carry(C_FA_25));
  Full_adder full_adder_8 (.A(PP6[13]), .B(C_FA_24B), .Cin(S_FA_25), .Sum(S_FA_25B), .Carry(C_FA_25B));
  Full_adder full_adder_9 (
    .A(full_adder_12_carry), .B(PP5[15]), .Cin(S_FA_25B), .Sum(half_adder_22_sum[25]),
    .Carry(full_adder_9_carry));
  Full_adder full_adder_10 (.A(PP5[14]), .B(PP6[12]), .Cin(PP7[10]), .Sum(S_FA_24), .Carry(C_FA_24));
  Full_adder full_adder_11 (.A(S_HA_24), .B(S_FA_24), .Cin(C_FA1_23B), .Sum(S_FA_24B), .Carry(C_FA_24B));
  Full_adder full_adder_12 (
    .A(full_adder_16_carry), .B(S_FA_24B), .Cin(PP4[16]), .Sum(half_adder_22_sum[24]),
    .Carry(full_adder_12_carry));
  Half_adder half_adder_4 (.A(C_FA2_23A), .B(C_FA1_23A), .Sum(S_HA_24), .Carry(C_HA_24));
  Full_adder full_adder_13 (.A(PP6[11]), .B(PP7[9]), .Cin(C_HA_22), .Sum(S_FA1_23A), .Carry(C_FA1_23A));
  Full_adder full_adder_14 (.A(C_FA2_22A), .B(PP5[13]), .Cin(C_FA1_22A), .Sum(S_FA2_23A), .Carry(C_FA2_23A));
  Full_adder full_adder_15 (.A(S_FA2_23A), .B(S_FA1_23A), .Cin(C_FA1_22B), .Sum(S_FA1_23B), .Carry(C_FA1_23B));
  Full_adder full_adder_16 (
    .A(full_adder_19_carry), .B(S_FA1_23B), .Cin(PP4[15]), .Sum(half_adder_22_sum[23]),
    .Carry(full_adder_16_carry));
  Half_adder half_adder_5 (.A(PP7[8]), .B(C_FA_21), .Sum(S_HA_22), .Carry(C_HA_22));
  Full_adder full_adder_17 (.A(PP5[12]), .B(PP6[10]), .Cin(S_HA_22), .Sum(S_FA1_22A), .Carry(C_FA1_22A));
  Full_adder full_adder_18 (.A(S_FA2_22A), .B(S_FA1_22A), .Cin(C_FA1_21B), .Sum(S_FA1_22B), .Carry(C_FA1_22B));
  Full_adder full_adder_19 (
    .A(full_adder_24_carry), .B(S_FA1_22B), .Cin(PP3[16]), .Sum(half_adder_22_sum[22]),
    .Carry(full_adder_19_carry));
  Full_adder full_adder_20 (.A(PP4[14]), .B(C_FA2_21A), .Cin(C_FA1_21A), .Sum(S_FA2_22A), .Carry(C_FA2_22A));
  Full_adder full_adder_21 (.A(C_HA_20), .B(PP7[7]), .Cin(C_FA_20), .Sum(S_FA_21), .Carry(C_FA_21));
  Full_adder full_adder_22 (.A(PP6[9]), .B(PP5[11]), .Cin(S_FA_21), .Sum(S_FA1_21A), .Carry(C_FA1_21A));
  Full_adder full_adder_23 (.A(S_FA2_21A), .B(S_FA1_21A), .Cin(C_FA1_20B), .Sum(S_FA1_21B), .Carry(C_FA1_21B));
  Full_adder full_adder_24 (
    .A(full_adder_29_carry), .B(S_FA1_21B), .Cin(PP3[15]), .Sum(half_adder_22_sum[21]),
    .Carry(full_adder_24_carry));
  Full_adder full_adder_25 (.A(PP4[13]), .B(C_FA2_20A), .Cin(C_FA1_20A), .Sum(S_FA2_21A), .Carry(C_FA2_21A));
  not not_1 (not_8_out[31], PP7[16]);
  Full_adder full_adder_26 (.A(C_FA2_15), .B(PP7[6]), .Cin(C_FA1_19), .Sum(S_FA_20), .Carry(C_FA_20));
  Half_adder half_adder_6 (.A(PP5[10]), .B(PP6[8]), .Sum(S_HA_20), .Carry(C_HA_20));
  Full_adder full_adder_27 (.A(PP4[12]), .B(S_HA_20), .Cin(S_FA_20), .Sum(S_FA1_20A), .Carry(C_FA1_20A));
  Full_adder full_adder_28 (.A(S_FA2_20A), .B(S_FA1_20A), .Cin(C_FA1_19B), .Sum(S_FA1_20B), .Carry(C_FA1_20B));
  Full_adder full_adder_29 (
    .A(full_adder_35_carry), .B(PP2[16]), .Cin(S_FA1_20B), .Sum(half_adder_22_sum[20]),
    .Carry(full_adder_29_carry));
  not not_2 (not_8_out[29], PP6[16]);
  Full_adder full_adder_30 (.A(PP3[14]), .B(C_FA2_19A), .Cin(C_FA1_19A), .Sum(S_FA2_20A), .Carry(C_FA2_20A));
  not not_3 (not_8_out[27], PP5[16]);
  Full_adder full_adder_31 (.A(C_FA2_18), .B(C_HA_18), .Cin(C_FA1_18), .Sum(S_FA1_19), .Carry(C_FA1_19));
  Full_adder full_adder_32 (.A(PP5[9]), .B(PP6[7]), .Cin(PP7[5]), .Sum(S_FA2_19), .Carry(C_FA2_19));
  Full_adder full_adder_33 (.A(PP4[11]), .B(S_FA2_19), .Cin(S_FA1_19), .Sum(S_FA1_19A), .Carry(C_FA1_19A));
  Full_adder full_adder_34 (.A(C_FA1_18B), .B(S_FA2_19A), .Cin(S_FA1_19A), .Sum(S_FA1_19B), .Carry(C_FA1_19B));
  Full_adder full_adder_35 (
    .A(full_adder_41_carry), .B(PP2[15]), .Cin(S_FA1_19B), .Sum(half_adder_22_sum[19]),
    .Carry(full_adder_35_carry));
  not not_4 (not_8_out[25], PP4[16]);
  Full_adder full_adder_36 (.A(PP3[13]), .B(C_FA2_18A), .Cin(C_FA1_18A), .Sum(S_FA2_19A), .Carry(C_FA2_19A));
  not not_5 (not_8_out[23], PP3[16]);
  not not_6 (not_8_out[21], PP2[16]);
  Full_adder full_adder_37 (.A(C_FA2_17), .B(C_FA3_17), .Cin(C_FA1_17), .Sum(S_FA1_18), .Carry(C_FA1_18));
  Full_adder full_adder_38 (.A(PP5[8]), .B(PP6[6]), .Cin(PP7[4]), .Sum(S_FA2_18), .Carry(C_FA2_18));
  Half_adder half_adder_7 (.A(PP3[12]), .B(PP4[10]), .Sum(S_HA_18), .Carry(C_HA_18));
  Full_adder full_adder_39 (.A(S_HA_18), .B(S_FA2_18), .Cin(S_FA1_18), .Sum(S_FA1_18A), .Carry(C_FA1_18A));
  Full_adder full_adder_40 (.A(C_FA1_17B), .B(S_FA2_18A), .Cin(S_FA1_18A), .Sum(S_FA1_18B), .Carry(C_FA1_18B));
  Full_adder full_adder_41 (
    .A(full_adder_48_carry), .B(PP1[16]), .Cin(S_FA1_18B), .Sum(half_adder_22_sum[18]),
    .Carry(full_adder_41_carry));
  Full_adder full_adder_42 (.A(PP2[14]), .B(C_FA1_17A), .Cin(C_FA2_17A), .Sum(S_FA2_18A), .Carry(C_FA2_18A));
  not not_7 (not_8_out[19], PP1[16]);
  not not_8 (not_8_out[17], PP0[16]);
  Full_adder full_adder_43 (.A(C_FA2_16), .B(C_HA_16), .Cin(C_FA1_16), .Sum(S_FA1_17), .Carry(C_FA1_17));
  Full_adder full_adder_44 (.A(PP6[5]), .B(PP7[3]), .Cin(1'b1), .Sum(S_FA2_17), .Carry(C_FA2_17));
  Full_adder full_adder_45 (.A(PP3[11]), .B(PP4[9]), .Cin(PP5[7]), .Sum(S_FA3_17), .Carry(C_FA3_17));
  Full_adder full_adder_46 (.A(S_FA3_17), .B(S_FA2_17), .Cin(S_FA1_17), .Sum(S_FA1_17A), .Carry(C_FA1_17A));
  Full_adder full_adder_47 (.A(C_FA1_16B), .B(S_FA2_17A), .Cin(S_FA1_17A), .Sum(S_FA1_17B), .Carry(C_FA1_17B));
  Full_adder full_adder_48 (
    .A(full_adder_54_carry), .B(PP1[15]), .Cin(S_FA1_17B), .Sum(half_adder_22_sum[17]),
    .Carry(full_adder_48_carry));
  Full_adder full_adder_49 (.A(PP2[13]), .B(C_FA2_16A), .Cin(C_FA1_16A), .Sum(S_FA2_17A), .Carry(C_FA2_17A));
  Full_adder full_adder_50 (.A(C_FA2_15), .B(C_HA_15), .Cin(C_FA1_15), .Sum(S_FA1_16), .Carry(C_FA1_16));
  Full_adder full_adder_51 (.A(PP5[6]), .B(PP6[4]), .Cin(PP7[2]), .Sum(S_FA2_16), .Carry(C_FA2_16));
  Half_adder half_adder_8 (.A(PP3[10]), .B(PP4[8]), .Sum(S_HA_16), .Carry(C_HA_16));
  Full_adder full_adder_52 (.A(S_HA_16), .B(S_FA2_16), .Cin(S_FA1_16), .Sum(S_FA1_16A), .Carry(C_FA1_16A));
  Full_adder full_adder_53 (.A(C_FA1_15B), .B(S_FA2_16A), .Cin(S_FA1_16A), .Sum(S_FA1_16B), .Carry(C_FA1_16B));
  Full_adder full_adder_54 (
    .A(full_adder_61_carry), .B(PP1[14]), .Cin(S_FA1_16B), .Sum(half_adder_22_sum[16]),
    .Carry(full_adder_54_carry));
  Full_adder full_adder_55 (.A(PP2[12]), .B(C_FA2_15A), .Cin(C_FA1_15A), .Sum(S_FA2_16A), .Carry(C_FA2_16A));
  Full_adder full_adder_56 (.A(C_FA2_14), .B(C_HA_14), .Cin(C_FA1_14), .Sum(S_FA1_15), .Carry(C_FA1_15));
  Full_adder full_adder_57 (.A(PP5[5]), .B(PP6[3]), .Cin(PP7[1]), .Sum(S_FA2_15), .Carry(C_FA2_15));
  Half_adder half_adder_9 (.A(PP3[9]), .B(PP4[7]), .Sum(S_HA_15), .Carry(C_HA_15));
  Full_adder full_adder_58 (.A(S_HA_15), .B(C_FA2_14A), .Cin(C_FA1_14A), .Sum(S_FA1_15A), .Carry(C_FA1_15A));
  Full_adder full_adder_59 (.A(PP2[11]), .B(S_FA2_15), .Cin(S_FA1_15), .Sum(S_FA2_15A), .Carry(C_FA2_15A));
  Full_adder full_adder_60 (.A(C_FA1_14B), .B(S_FA2_15A), .Cin(S_FA1_15A), .Sum(S_FA1_15B), .Carry(C_FA1_15B));
  Full_adder full_adder_61 (
    .A(full_adder_67_carry), .B(PP1[13]), .Cin(S_FA1_15B), .Sum(half_adder_22_sum[15]),
    .Carry(full_adder_61_carry));
  Full_adder full_adder_62 (.A(N_7), .B(C_HA_13), .Cin(C_FA_13), .Sum(S_FA1_14), .Carry(C_FA1_14));
  Full_adder full_adder_63 (.A(PP5[4]), .B(PP6[2]), .Cin(PP7[0]), .Sum(S_FA2_14), .Carry(C_FA2_14));
  Half_adder half_adder_10 (.A(PP3[8]), .B(PP4[6]), .Sum(S_HA_14), .Carry(C_HA_14));
  Full_adder full_adder_64 (.A(S_HA_14), .B(C_FA2_13A), .Cin(C_FA1_13A), .Sum(S_FA1_14A), .Carry(C_FA1_14A));
  Full_adder full_adder_65 (.A(PP2[10]), .B(S_FA2_14), .Cin(S_FA1_14), .Sum(S_FA2_14A), .Carry(C_FA2_14A));
  Full_adder full_adder_66 (.A(C_FA1_13B), .B(S_FA2_14A), .Cin(S_FA1_14A), .Sum(S_FA1_14B), .Carry(C_FA1_14B));
  Full_adder full_adder_67 (
    .A(full_adder_71_carry), .B(PP1[12]), .Cin(S_FA1_14B), .Sum(half_adder_22_sum[14]),
    .Carry(full_adder_67_carry));
  Full_adder full_adder_68 (.A(PP6[1]), .B(C_HA_12), .Cin(C_FA_12), .Sum(S_FA_13), .Carry(C_FA_13));
  Half_adder half_adder_11 (.A(PP4[5]), .B(PP5[3]), .Sum(S_HA_13), .Carry(C_HA_13));
  Full_adder full_adder_69 (.A(S_FA_13), .B(C_FA2_12A), .Cin(C_FA1_12A), .Sum(S_FA1_13A), .Carry(C_FA1_13A));
  Full_adder full_adder_70 (.A(C_FA1_12B), .B(S_FA2_13A), .Cin(S_FA1_13A), .Sum(S_FA1_13B), .Carry(C_FA1_13B));
  Full_adder full_adder_71 (
    .A(full_adder_77_carry), .B(PP1[11]), .Cin(S_FA1_13B), .Sum(half_adder_22_sum[13]),
    .Carry(full_adder_71_carry));
  Adder #(.width(32)) adder_1 (
    .a({C_HA_30, half_adder_22_sum, 1'b0, N_0}),
    .b({not_8_out[31], 1'b1, not_8_out[29], 1'b1, not_8_out[27], 1'b1, not_8_out[25], 1'b1, not_8_out[23], 1'b1, not_8_out[21], 1'b1, not_8_out[19], 1'b1, not_8_out[17], PP0}),
    .out(Product), .cin(1'b0), .cout(out_12));
  Full_adder full_adder_72 (.A(S_HA_13), .B(PP2[9]), .Cin(PP3[7]), .Sum(S_FA2_13A), .Carry(C_FA2_13A));
  Full_adder full_adder_73 (.A(PP5[2]), .B(PP6[0]), .Cin(N_6), .Sum(S_FA_12), .Carry(C_FA_12));
  Half_adder half_adder_12 (.A(PP4[4]), .B(C_HA_11), .Sum(S_HA_12), .Carry(C_HA_12));
  Full_adder full_adder_74 (.A(S_FA_12), .B(C_FA2_11A), .Cin(C_FA1_11A), .Sum(S_FA1_12A), .Carry(C_FA1_12A));
  Full_adder full_adder_75 (.A(S_HA_12), .B(PP2[8]), .Cin(PP3[6]), .Sum(S_FA2_12A), .Carry(C_FA2_12A));
  Full_adder full_adder_76 (.A(C_FA1_11B), .B(S_FA2_12A), .Cin(S_FA1_12A), .Sum(S_FA1_12B), .Carry(C_FA1_12B));
  Full_adder full_adder_77 (
    .A(full_adder_80_carry), .B(PP1[10]), .Cin(S_FA1_12B), .Sum(half_adder_22_sum[12]),
    .Carry(full_adder_77_carry));
  Half_adder half_adder_13 (.A(PP5[1]), .B(C_HA_10), .Sum(S_HA_11), .Carry(C_HA_11));
  Full_adder full_adder_78 (.A(S_HA_11), .B(C_FA2_10A), .Cin(C_FA1_10A), .Sum(S_FA1_11A), .Carry(C_FA1_11A));
  Full_adder full_adder_79 (.A(C_FA1_10B), .B(S_FA2_11A), .Cin(S_FA1_11A), .Sum(S_FA1_11B), .Carry(C_FA1_11B));
  Full_adder full_adder_80 (
    .A(full_adder_85_carry), .B(PP1[9]), .Cin(S_FA1_11B), .Sum(half_adder_22_sum[11]),
    .Carry(full_adder_80_carry));
  Full_adder full_adder_81 (.A(PP2[7]), .B(PP3[5]), .Cin(PP4[3]), .Sum(S_FA2_11A), .Carry(C_FA2_11A));
  Half_adder half_adder_14 (.A(PP5[0]), .B(N_5), .Sum(S_HA_10), .Carry(C_HA_10));
  Full_adder full_adder_82 (.A(PP3[4]), .B(PP4[2]), .Cin(S_HA_10), .Sum(S_FA1_10A), .Carry(C_FA1_10A));
  Full_adder full_adder_83 (.A(C_HA_9), .B(C_FA1_9), .Cin(PP2[6]), .Sum(S_FA2_10A), .Carry(C_FA2_10A));
  Full_adder full_adder_84 (.A(C_FA_9), .B(S_FA2_10A), .Cin(S_FA1_10A), .Sum(S_FA1_10B), .Carry(C_FA1_10B));
  Full_adder full_adder_85 (
    .A(full_adder_88_carry), .B(PP1[8]), .Cin(S_FA1_10B), .Sum(half_adder_22_sum[10]),
    .Carry(full_adder_85_carry));
  Full_adder full_adder_86 (.A(PP4[1]), .B(C_HA_8), .Cin(C_FA1_8), .Sum(S_FA1_9), .Carry(C_FA1_9));
  Half_adder half_adder_15 (.A(PP2[5]), .B(PP3[3]), .Sum(S_HA_9), .Carry(C_HA_9));
  Full_adder full_adder_87 (.A(S_HA_9), .B(C_FA_8), .Cin(S_FA1_9), .Sum(S_FA_9), .Carry(C_FA_9));
  Full_adder full_adder_88 (
    .A(PP1[7]), .B(full_adder_91_carry), .Cin(S_FA_9), .Sum(half_adder_22_sum[9]), .Carry(full_adder_88_carry));
  Full_adder full_adder_89 (.A(PP3[2]), .B(PP4[0]), .Cin(N_4), .Sum(S_FA1_8), .Carry(C_FA1_8));
  Half_adder half_adder_16 (.A(PP2[4]), .B(C_HA_7), .Sum(S_HA_8), .Carry(C_HA_8));
  Full_adder full_adder_90 (.A(C_FA_7), .B(S_FA1_8), .Cin(S_HA_8), .Sum(S_FA_8), .Carry(C_FA_8));
  Full_adder full_adder_91 (
    .A(full_adder_93_carry), .B(S_FA_8), .Cin(PP1[6]), .Sum(half_adder_22_sum[8]), .Carry(full_adder_91_carry));
  Half_adder half_adder_17 (.A(PP3[1]), .B(C_HA_6), .Sum(S_HA_7), .Carry(C_HA_7));
  Full_adder full_adder_92 (.A(PP2[3]), .B(C_FA_6), .Cin(S_HA_7), .Sum(S_FA_7), .Carry(C_FA_7));
  Full_adder full_adder_93 (
    .A(PP1[5]), .B(full_adder_95_carry), .Cin(S_FA_7), .Sum(half_adder_22_sum[7]), .Carry(full_adder_93_carry));
  Half_adder half_adder_18 (.A(PP3[0]), .B(N_3), .Sum(S_HA_6), .Carry(C_HA_6));
  Full_adder full_adder_94 (.A(C_HA_5), .B(PP2[2]), .Cin(S_HA_6), .Sum(S_FA_6), .Carry(C_FA_6));
  Full_adder full_adder_95 (
    .A(full_adder_96_carry), .B(PP1[4]), .Cin(S_FA_6), .Sum(half_adder_22_sum[6]), .Carry(full_adder_95_carry));
  Half_adder half_adder_19 (.A(PP2[1]), .B(C_HA_4), .Sum(S_HA_5), .Carry(C_HA_5));
  Full_adder full_adder_96 (
    .A(full_adder_97_carry), .B(PP1[3]), .Cin(S_HA_5), .Sum(half_adder_22_sum[5]), .Carry(full_adder_96_carry));
  Half_adder half_adder_20 (.A(PP2[0]), .B(N_2), .Sum(S_HA_4), .Carry(C_HA_4));
  Full_adder full_adder_97 (
    .A(half_adder_21_carry), .B(PP1[2]), .Cin(S_HA_4), .Sum(half_adder_22_sum[4]), .Carry(full_adder_97_carry));
  Half_adder half_adder_21 (
    .A(PP1[1]), .B(half_adder_22_carry), .Sum(half_adder_22_sum[3]), .Carry(half_adder_21_carry));
  Half_adder half_adder_22 (.A(PP1[0]), .B(N_1), .Sum(half_adder_22_sum[2]), .Carry(half_adder_22_carry));

  // Other names for the same wires on the sheet: PP_0_0 = PP0[0]; PP_0_1 = PP0[1]; PP_0_2 = PP0[2]; PP_0_3 = PP0[3];
  //   PP_0_4 = PP0[4]; PP_0_5 = PP0[5]; PP_0_6 = PP0[6]; PP_0_7 = PP0[7]; PP_0_8 = PP0[8]; PP_0_9 = PP0[9];
  //   PP_0_10 = PP0[10]; PP_0_11 = PP0[11]; PP_0_12 = PP0[12]; PP_0_13 = PP0[13]; PP_0_14 = PP0[14];
  //   PP_0_15 = PP0[15]; PP_0_16 = PP0[16]; PP_1_0 = PP1[0]; PP_1_1 = PP1[1]; PP_1_2 = PP1[2]; PP_1_3 = PP1[3];
  //   PP_1_4 = PP1[4]; PP_1_5 = PP1[5]; PP_1_6 = PP1[6]; PP_1_7 = PP1[7]; PP_1_8 = PP1[8]; PP_1_9 = PP1[9];
  //   PP_1_10 = PP1[10]; PP_1_11 = PP1[11]; PP_1_12 = PP1[12]; PP_1_13 = PP1[13]; PP_1_14 = PP1[14];
  //   PP_1_15 = PP1[15]; PP_1_16 = PP1[16]; PP_2_0 = PP2[0]; PP_2_1 = PP2[1]; PP_2_2 = PP2[2]; PP_2_3 = PP2[3];
  //   PP_2_4 = PP2[4]; PP_2_5 = PP2[5]; PP_2_6 = PP2[6]; PP_2_7 = PP2[7]; PP_2_8 = PP2[8]; PP_2_9 = PP2[9];
  //   PP_2_10 = PP2[10]; PP_2_11 = PP2[11]; PP_2_12 = PP2[12]; PP_2_13 = PP2[13]; PP_2_14 = PP2[14];
  //   PP_2_15 = PP2[15]; PP_2_16 = PP2[16]; PP_3_0 = PP3[0]; PP_3_1 = PP3[1]; PP_3_2 = PP3[2]; PP_3_3 = PP3[3];
  //   PP_3_4 = PP3[4]; PP_3_5 = PP3[5]; PP_3_6 = PP3[6]; PP_3_7 = PP3[7]; PP_3_8 = PP3[8]; PP_3_9 = PP3[9];
  //   PP_3_10 = PP3[10]; PP_3_11 = PP3[11]; PP_3_12 = PP3[12]; PP_3_13 = PP3[13]; PP_3_14 = PP3[14];
  //   PP_3_15 = PP3[15]; PP_3_16 = PP3[16]; PP_4_0 = PP4[0]; PP_4_1 = PP4[1]; PP_4_2 = PP4[2]; PP_4_3 = PP4[3];
  //   PP_4_4 = PP4[4]; PP_4_5 = PP4[5]; PP_4_6 = PP4[6]; PP_4_7 = PP4[7]; PP_4_8 = PP4[8]; PP_4_9 = PP4[9];
  //   PP_4_10 = PP4[10]; PP_4_11 = PP4[11]; PP_4_12 = PP4[12]; PP_4_13 = PP4[13]; PP_4_14 = PP4[14];
  //   PP_4_15 = PP4[15]; PP_4_16 = PP4[16]; PP_5_0 = PP5[0]; PP_5_1 = PP5[1]; PP_5_2 = PP5[2]; PP_5_3 = PP5[3];
  //   PP_5_4 = PP5[4]; PP_5_5 = PP5[5]; PP_5_6 = PP5[6]; PP_5_7 = PP5[7]; PP_5_8 = PP5[8]; PP_5_9 = PP5[9];
  //   PP_5_10 = PP5[10]; PP_5_11 = PP5[11]; PP_5_12 = PP5[12]; PP_5_13 = PP5[13]; PP_5_14 = PP5[14];
  //   PP_5_15 = PP5[15]; PP_5_16 = PP5[16]; PP_6_0 = PP6[0]; PP_6_1 = PP6[1]; PP_6_2 = PP6[2]; PP_6_3 = PP6[3];
  //   PP_6_4 = PP6[4]; PP_6_5 = PP6[5]; PP_6_6 = PP6[6]; PP_6_7 = PP6[7]; PP_6_8 = PP6[8]; PP_6_9 = PP6[9];
  //   PP_6_10 = PP6[10]; PP_6_11 = PP6[11]; PP_6_12 = PP6[12]; PP_6_13 = PP6[13]; PP_6_14 = PP6[14];
  //   PP_6_15 = PP6[15]; PP_6_16 = PP6[16]; PP_7_0 = PP7[0]; PP_7_1 = PP7[1]; PP_7_2 = PP7[2]; PP_7_3 = PP7[3];
  //   PP_7_4 = PP7[4]; PP_7_5 = PP7[5]; PP_7_6 = PP7[6]; PP_7_7 = PP7[7]; PP_7_8 = PP7[8]; PP_7_9 = PP7[9];
  //   PP_7_10 = PP7[10]; PP_7_11 = PP7[11]; PP_7_12 = PP7[12]; PP_7_13 = PP7[13]; PP_7_14 = PP7[14];
  //   PP_7_15 = PP7[15]; PP_7_16 = PP7[16]; Y_bus[15:0] = Y
endmodule

module Full_adder (
  input  A,
  input  B,
  input  Cin,
  output Sum,
  output Carry
);

  wire half_adder_1_carry, half_adder_1_sum, half_adder_2_carry;

  Half_adder half_adder_1 (.A(A), .B(B), .Sum(half_adder_1_sum), .Carry(half_adder_1_carry));
  Half_adder half_adder_2 (.A(half_adder_1_sum), .B(Cin), .Sum(Sum), .Carry(half_adder_2_carry));
  or or_1 (Carry, half_adder_2_carry, half_adder_1_carry);
endmodule

module Booth_row_generator (
  input  Y_high,
  input  Y,
  input  Y_low,
  input  [15:0] X,
  output Neg,
  output [16:0] PP
);

  wire booth_encoder_1_x1, booth_encoder_1_x2;

  Booth_encoder booth_encoder_1 (
    .Y_up(Y_high), .Y(Y), .Y_down(Y_low), .Neg(Neg), .X1(booth_encoder_1_x1), .X2(booth_encoder_1_x2));
  Booth_selector_1bit booth_selector_1bit_1 (
    .X_current(X[0]), .X_previous(1'b0), .X2(booth_encoder_1_x2), .X1(booth_encoder_1_x1), .Neg(Neg),
    .PP_bit(PP[0]));
  Booth_selector_1bit booth_selector_1bit_2 (
    .X_current(X[1]), .X_previous(X[0]), .X2(booth_encoder_1_x2), .X1(booth_encoder_1_x1), .Neg(Neg),
    .PP_bit(PP[1]));
  Booth_selector_1bit booth_selector_1bit_3 (
    .X_current(X[2]), .X_previous(X[1]), .X2(booth_encoder_1_x2), .X1(booth_encoder_1_x1), .Neg(Neg),
    .PP_bit(PP[2]));
  Booth_selector_1bit booth_selector_1bit_4 (
    .X_current(X[3]), .X_previous(X[2]), .X2(booth_encoder_1_x2), .X1(booth_encoder_1_x1), .Neg(Neg),
    .PP_bit(PP[3]));
  Booth_selector_1bit booth_selector_1bit_5 (
    .X_current(X[4]), .X_previous(X[3]), .X2(booth_encoder_1_x2), .X1(booth_encoder_1_x1), .Neg(Neg),
    .PP_bit(PP[4]));
  Booth_selector_1bit booth_selector_1bit_6 (
    .X_current(X[5]), .X_previous(X[4]), .X2(booth_encoder_1_x2), .X1(booth_encoder_1_x1), .Neg(Neg),
    .PP_bit(PP[5]));
  Booth_selector_1bit booth_selector_1bit_7 (
    .X_current(X[6]), .X_previous(X[5]), .X2(booth_encoder_1_x2), .X1(booth_encoder_1_x1), .Neg(Neg),
    .PP_bit(PP[6]));
  Booth_selector_1bit booth_selector_1bit_8 (
    .X_current(X[7]), .X_previous(X[6]), .X2(booth_encoder_1_x2), .X1(booth_encoder_1_x1), .Neg(Neg),
    .PP_bit(PP[7]));
  Booth_selector_1bit booth_selector_1bit_9 (
    .X_current(X[8]), .X_previous(X[7]), .X2(booth_encoder_1_x2), .X1(booth_encoder_1_x1), .Neg(Neg),
    .PP_bit(PP[8]));
  Booth_selector_1bit booth_selector_1bit_10 (
    .X_current(X[9]), .X_previous(X[8]), .X2(booth_encoder_1_x2), .X1(booth_encoder_1_x1), .Neg(Neg),
    .PP_bit(PP[9]));
  Booth_selector_1bit booth_selector_1bit_11 (
    .X_current(X[10]), .X_previous(X[9]), .X2(booth_encoder_1_x2), .X1(booth_encoder_1_x1), .Neg(Neg),
    .PP_bit(PP[10]));
  Booth_selector_1bit booth_selector_1bit_12 (
    .X_current(X[11]), .X_previous(X[10]), .X2(booth_encoder_1_x2), .X1(booth_encoder_1_x1), .Neg(Neg),
    .PP_bit(PP[11]));
  Booth_selector_1bit booth_selector_1bit_13 (
    .X_current(X[12]), .X_previous(X[11]), .X2(booth_encoder_1_x2), .X1(booth_encoder_1_x1), .Neg(Neg),
    .PP_bit(PP[12]));
  Booth_selector_1bit booth_selector_1bit_14 (
    .X_current(X[13]), .X_previous(X[12]), .X2(booth_encoder_1_x2), .X1(booth_encoder_1_x1), .Neg(Neg),
    .PP_bit(PP[13]));
  Booth_selector_1bit booth_selector_1bit_15 (
    .X_current(X[14]), .X_previous(X[13]), .X2(booth_encoder_1_x2), .X1(booth_encoder_1_x1), .Neg(Neg),
    .PP_bit(PP[14]));
  Booth_selector_1bit booth_selector_1bit_16 (
    .X_current(X[15]), .X_previous(X[14]), .X2(booth_encoder_1_x2), .X1(booth_encoder_1_x1), .Neg(Neg),
    .PP_bit(PP[15]));
  Booth_selector_1bit booth_selector_1bit_17 (
    .X_current(X[15]), .X_previous(X[15]), .X2(booth_encoder_1_x2), .X1(booth_encoder_1_x1), .Neg(Neg),
    .PP_bit(PP[16]));
endmodule

module Booth_encoder (
  input  Y_up,
  input  Y,
  input  Y_down,
  output Neg,
  output X1,
  output X2
);

  wire and_1_out, and_2_out, not_1_out, not_2_out, not_3_out;

  not not_1 (not_1_out, Y);
  not not_2 (not_2_out, Y_up);
  not not_3 (not_3_out, Y_down);
  xor xor_1 (X1, Y_down, Y);
  and and_1 (and_1_out, Y_up, not_1_out, not_3_out);
  and and_2 (and_2_out, not_2_out, Y, Y_down);
  or or_1 (X2, and_1_out, and_2_out);

  assign Neg = Y_up;
endmodule

module Booth_selector_1bit (
  input  X_current,
  input  X_previous,
  input  X2,
  input  X1,
  input  Neg,
  output PP_bit
);

  wire and_1_out, multiplexer_1_out, or_1_out;

  Multiplexer multiplexer_1 (.in0(X_current), .in1(X_previous), .out(multiplexer_1_out), .sel(X2));
  or or_1 (or_1_out, X2, X1);
  and and_1 (and_1_out, multiplexer_1_out, or_1_out);
  xor xor_1 (PP_bit, and_1_out, Neg);
endmodule

module Half_adder (
  input  A,
  input  B,
  output Sum,
  output Carry
);

  xor xor_1 (Sum, A, B);
  and and_1 (Carry, B, A);
endmodule

module test (
  input  [2:0] Y,
  input  [15:0] X,
  output Neg_out,
  output [16:0] PP_row
);

  Booth_row_generator booth_row_generator_1 (.Y_high(Y[2]), .Y(Y[1]), .Y_low(Y[0]), .X(X), .Neg(Neg_out), .PP(PP_row));
endmodule

module TEST2 (
  input  [15:0] X,
  input  [15:0] Y,
  output [16:0] PP0,
  output [16:0] PP1,
  output [16:0] PP2,
  output [16:0] PP3,
  output [16:0] PP4,
  output [16:0] PP5,
  output [16:0] PP6,
  output [16:0] PP7,
  output [31:0] Product,
  output Carry
);

  main main_1 (
    .X(X), .Y(Y), .PP0(PP0), .PP1(PP1), .PP2(PP2), .PP3(PP3), .PP4(PP4), .PP5(PP5), .PP6(PP6), .PP7(PP7),
    .Product(Product), .out_12(Carry));
endmodule
